# Fritzing sketch fire (saved by Fritzing 0.9.0b)

parts:
  Part1 = Arduino Pro Mini v13
  NEOPIXEL1 = Neopixel Strip -- Black (30/m)
  C1 = Electrolytic Capacitor [capacitance=0.22mF voltage=10V package="100 mil [THT, electrolytic]"]
  IR1 = TSOP312.., 314.. [package=THT]
  S1 = Momentary Switch [package=tactile-pth]
  R3 = Resistor [tolerance=±5% resistance=330 package="0603 [SMD]"]
  R2 = Resistor [tolerance=±5% resistance=15k package="0603 [SMD]"]
  R1 = Resistor [tolerance=±5% resistance=220k package="0603 [SMD]"]
  JACK1 = 2.1mm Barrel Jack with Terminal Block
  J1 = Piezo Speaker

nets:
  N1: Part1.GND, C1.-, IR1.Vs, S1.1, R1.Pin_1, JACK1.NEG, J1.pin1
  N2: Part1.VCC, NEOPIXEL1.DI, C1.+, IR1.Data, R2.Pin_1, JACK1.POS
  N3: Part1.D8, J1.pin2
  N4: Part1.D5_PWM, IR1.GND
  N5: Part1.D4, R3.Pin_1
  N6: Part1.D2, R2.Pin_0
  N7: NEOPIXEL1.+5V, R3.Pin_0
  N8: S1.2, R1.Pin_0

notes:
  1. IR and button goes to the top right part of the hannukia
  2. Leds strip goes beneath the hot glue
  3. The rest goes on a PCB hidden in the back
  To 5V Battery

custom parts:
  Neopixel Strip -- Black (30/m): Neopixel Strip, Black, 30 pixels per meter.
